// Digital circuit FA.dig as structural Verilog
module FA (
  input  B,
  input  A,
  input  cin,
  output S,
  output Co
);

  wire and_1_out, and_2_out, and_3_out, xor_1_out;

  and and_1 (and_1_out, B, cin);
  and and_2 (and_2_out, A, cin);
  or or_1 (Co, and_3_out, and_2_out, and_1_out);
  and and_3 (and_3_out, A, B);
  xor xor_1 (xor_1_out, A, B);
  xor xor_2 (S, xor_1_out, cin);
endmodule
