// Digital circuit OpenCode.dig as structural Verilog
module OpenCode (
  input  [31:0] in,
  output [15:0] CONST,
  output [3:0] C,
  output [3:0] B,
  output [3:0] A,
  output [3:0] OP
);


  assign A = in[27:24];
  assign B = in[23:20];
  assign C = in[19:16];
  assign CONST = in[15:0];
  assign OP = in[31:28];
endmodule
