// Digital circuit ShiftLeft.dig as structural Verilog
module ShiftLeft (
  input  [31:0] A,
  input  [31:0] B,
  output [31:0] S
);

  wire or_1_out;
  wire [31:0] shftleft_2bits_1_s, shifterleft_1bit_1_s, shiftleft_4bits_1_s, shiftleft_8bits_1_s,
       shiftleft_16bits_1_s;

  shifterLeft_1bit shifterleft_1bit_1 (.A(A), .B(B[0]), .S(shifterleft_1bit_1_s));
  shftLeft_2bits shftleft_2bits_1 (.A(shifterleft_1bit_1_s), .B(B[1]), .S(shftleft_2bits_1_s));
  or or_1 (or_1_out, B[5], B[6], B[7], B[8], B[9], B[10], B[11], B[12], B[13], B[14], B[15], B[16], B[17], B[18], B[19], B[20], B[21], B[22], B[23], B[24], B[25], B[26], B[27], B[28], B[29], B[30], B[31]);
  shiftLeft_4bits shiftleft_4bits_1 (.A(shftleft_2bits_1_s), .B(B[2]), .S(shiftleft_4bits_1_s));
  shiftLeft_8bits shiftleft_8bits_1 (.A(shiftleft_4bits_1_s), .B(B[3]), .S(shiftleft_8bits_1_s));
  shiftLeft_16bits shiftleft_16bits_1 (.A(shiftleft_8bits_1_s), .B(B[4]), .S(shiftleft_16bits_1_s));
  Multiplexer #(.Bits(32)) multiplexer_1 (.sel(or_1_out), .in_0(shiftleft_16bits_1_s), .in_1({32{1'b0}}), .out(S));
endmodule
