// Digital circuit ShiftRigth.dig as structural Verilog
module ShiftRigth (
  input  [31:0] A,
  input  [31:0] B,
  output [31:0] S
);

  wire or_1_out;
  wire [31:0] shfitrigth_2bits_1_s, shiftrigth_1bits_1_s, shiftrigth_4bits_1_s, shiftrigth_8bits_1_s,
       shiftrigth_16bits_1_s;

  shiftRigth_1Bits shiftrigth_1bits_1 (.A(A), .B(B[0]), .S(shiftrigth_1bits_1_s));
  or or_1 (or_1_out, B[5], B[6], B[7], B[8], B[9], B[10], B[11], B[12], B[13], B[14], B[15], B[16], B[17], B[18], B[19], B[20], B[21], B[22], B[23], B[24], B[25], B[26], B[27], B[28], B[29], B[30], B[31]);
  shfitRigth_2Bits shfitrigth_2bits_1 (.A(shiftrigth_1bits_1_s), .B(B[1]), .S(shfitrigth_2bits_1_s));
  shiftRigth_4bits shiftrigth_4bits_1 (.A(shfitrigth_2bits_1_s), .B(B[2]), .S(shiftrigth_4bits_1_s));
  shiftRigth_8bits shiftrigth_8bits_1 (.A(shiftrigth_4bits_1_s), .B(B[3]), .S(shiftrigth_8bits_1_s));
  shiftRigth_16bits shiftrigth_16bits_1 (.A(shiftrigth_8bits_1_s), .B(B[4]), .S(shiftrigth_16bits_1_s));
  Multiplexer #(.Bits(32)) multiplexer_1 (.sel(or_1_out), .in_0(shiftrigth_16bits_1_s), .in_1({32{1'b0}}), .out(S));
endmodule
