// Digital circuit Soma_4bits.dig as structural Verilog
module Soma_4bits (
  input  [3:0] A,
  input  [3:0] B,
  input  Cin,
  output [3:0] S,
  output Cout
);

  wire c0, c1, fa_1_co, fa_1_s, fa_2_co, fa_2_s, fa_3_co, fa_3_s, fa_4_co, fa_4_s, fa_5_co, fa_5_s, fa_6_co,
       fa_6_s, fa_7_s, fa_8_s;

  FA fa_1 (.B(B[0]), .A(A[0]), .cin(1'b0), .S(fa_1_s), .Co(fa_1_co));
  FA fa_2 (.B(B[0]), .A(A[0]), .cin(1'b1), .S(fa_2_s), .Co(fa_2_co));
  FA fa_3 (.B(B[1]), .A(A[1]), .cin(fa_1_co), .S(fa_3_s), .Co(fa_3_co));
  Multiplexer multiplexer_1 (.sel(Cin), .in_0(fa_1_s), .in_1(fa_2_s), .out(S[0]));
  FA fa_4 (.B(B[1]), .A(A[1]), .cin(fa_2_co), .S(fa_4_s), .Co(fa_4_co));
  FA fa_5 (.B(B[2]), .A(A[2]), .cin(fa_3_co), .S(fa_5_s), .Co(fa_5_co));
  Multiplexer multiplexer_2 (.sel(Cin), .in_0(fa_3_s), .in_1(fa_4_s), .out(S[1]));
  FA fa_6 (.B(B[2]), .A(A[2]), .cin(fa_4_co), .S(fa_6_s), .Co(fa_6_co));
  FA fa_7 (.B(B[3]), .A(A[3]), .cin(fa_5_co), .S(fa_7_s), .Co(c0));
  Multiplexer multiplexer_3 (.sel(Cin), .in_0(fa_5_s), .in_1(fa_6_s), .out(S[2]));
  FA fa_8 (.B(B[3]), .A(A[3]), .cin(fa_6_co), .S(fa_8_s), .Co(c1));
  Multiplexer multiplexer_4 (.sel(Cin), .in_0(fa_7_s), .in_1(fa_8_s), .out(S[3]));
  Multiplexer multiplexer_5 (.sel(Cin), .in_0(c0), .in_1(c1), .out(Cout));
endmodule
