// Digital circuit Somador_CarrySelect.dig as structural Verilog
module Somador_CarrySelect (
  input  [31:0] A,
  input  [31:0] B,
  output [31:0] S
);

  wire c0, c1, c2, c4, c5, c5b, c6, c6b, c7, c7b;
  wire [3:0] soma_4bits_1_s, soma_4bits_2_s, soma_4bits_3_s, soma_4bits_4_s, soma_4bits_5_s, soma_4bits_6_s,
       soma_4bits_7_s, soma_4bits_8_s;

  Soma_4bits soma_4bits_1 (.A(A[31:28]), .B(B[31:28]), .Cin(c7), .S(soma_4bits_1_s));  // open: Cout
  Soma_4bits soma_4bits_2 (.A(A[31:28]), .B(B[31:28]), .Cin(c7b), .S(soma_4bits_2_s));  // open: Cout
  Multiplexer #(.Bits(4)) multiplexer_1 (.sel(c4), .in_0(soma_4bits_1_s), .in_1(soma_4bits_2_s), .out(S[31:28]));
  Soma_4bits soma_4bits_3 (.A(A[27:24]), .B(B[27:24]), .Cin(c6b), .S(soma_4bits_3_s), .Cout(c7b));
  Soma_4bits soma_4bits_4 (.A(A[27:24]), .B(B[27:24]), .Cin(c6), .S(soma_4bits_4_s), .Cout(c7));
  Soma_4bits soma_4bits_5 (.A(A[23:20]), .B(B[23:20]), .Cin(c5b), .S(soma_4bits_5_s), .Cout(c6b));
  Multiplexer #(.Bits(4)) multiplexer_2 (.sel(c4), .in_0(soma_4bits_4_s), .in_1(soma_4bits_3_s), .out(S[27:24]));
  Soma_4bits soma_4bits_6 (.A(A[23:20]), .B(B[23:20]), .Cin(c5), .S(soma_4bits_6_s), .Cout(c6));
  Multiplexer #(.Bits(4)) multiplexer_3 (.sel(c4), .in_0(soma_4bits_6_s), .in_1(soma_4bits_5_s), .out(S[23:20]));
  Soma_4bits soma_4bits_7 (.A(A[19:16]), .B(B[19:16]), .Cin(1'b0), .S(soma_4bits_7_s), .Cout(c5));
  Soma_4bits soma_4bits_8 (.A(A[19:16]), .B(B[19:16]), .Cin(1'b1), .S(soma_4bits_8_s), .Cout(c5b));
  Multiplexer #(.Bits(4)) multiplexer_4 (.sel(c4), .in_0(soma_4bits_7_s), .in_1(soma_4bits_8_s), .out(S[19:16]));
  Soma_4bits soma_4bits_9 (.A(A[15:12]), .B(B[15:12]), .Cin(c2), .S(S[15:12]), .Cout(c4));
  Soma_4bits soma_4bits_10 (.A(A[11:8]), .B(B[11:8]), .Cin(c1), .S(S[11:8]), .Cout(c2));
  Soma_4bits soma_4bits_11 (.A(A[7:4]), .B(B[7:4]), .Cin(c0), .S(S[7:4]), .Cout(c1));
  Soma_4bits soma_4bits_12 (.A(A[3:0]), .B(B[3:0]), .Cin(1'b0), .S(S[3:0]), .Cout(c0));

  // Other names for the same wires on the sheet: a0[3:0] = A[3:0]; a1[3:0] = A[7:4]; a2[3:0] = A[11:8];
  //   a3[3:0] = A[15:12]; a4[3:0] = A[19:16]; a5[3:0] = A[23:20]; a6[3:0] = A[27:24]; a7[3:0] = A[31:28];
  //   b0[3:0] = B[3:0]; b1[3:0] = B[7:4]; b2[3:0] = B[11:8]; b3[3:0] = B[15:12]; b4[3:0] = B[19:16];
  //   b5[3:0] = B[23:20]; b6[3:0] = B[27:24]; b7[3:0] = B[31:28]; s0[3:0] = S[3:0]; s1[3:0] = S[7:4];
  //   s2[3:0] = S[11:8]; s3[3:0] = S[15:12]; s4[3:0] = S[19:16]; s5[3:0] = S[23:20]; s6[3:0] = S[27:24];
  //   s7[3:0] = S[31:28]
endmodule
