// Digital circuit ULA.dig as structural Verilog
module ULA (
  input  [31:0] A,
  input  [31:0] B,
  input  [2:0] sel,
  output [31:0] S,
  output zero
);

  wire [31:0] \and , \not , \or , ShiftLeft, ShiftRight, somador, subtrator, \xor ;

  Somador_CarrySelect somador_carryselect_1 (.A(A), .B(B), .S(somador));
  subtrator2 subtrator2_1 (.A(A), .B(B), .S(subtrator));
  assign \and  = A & B;  // And and_1, 32 bits wide
  assign \or  = A | B;  // Or or_1, 32 bits wide
  assign \xor  = A ^ B;  // XOr xor_1, 32 bits wide
  assign \not  = ~A;  // Not not_1, 32 bits wide
  ShiftLeft shiftleft_1 (.A(A), .B(B), .S(ShiftLeft));
  ShiftRigth shiftrigth_1 (.A(A), .B(B), .S(ShiftRight));
  Multiplexer #(.Selector_Bits(3), .Bits(32)) multiplexer_1 (
    .sel(sel), .in_0(somador), .in_1(subtrator), .in_2(\and ), .in_3(\or ), .in_4(\xor ), .in_5(\not ),
    .in_6(ShiftLeft), .in_7(ShiftRight), .out(S));
  nor nor_1 (zero, S[0], S[1], S[2], S[3], S[4], S[5], S[6], S[7], S[8], S[9], S[10], S[11], S[12], S[13], S[14], S[15], S[16], S[17], S[18], S[19], S[20], S[21], S[22], S[23], S[24], S[25], S[26], S[27], S[28], S[29], S[30], S[31]);
endmodule
