// Digital circuit shftLeft_2bits.dig as structural Verilog
module shftLeft_2bits (
  input  [31:0] A,
  input  B,
  output [31:0] S
);

  Multiplexer multiplexer_1 (.sel(B), .in_0(A[31]), .in_1(A[29]), .out(S[31]));
  Multiplexer multiplexer_2 (.sel(B), .in_0(A[30]), .in_1(A[28]), .out(S[31]));
  Multiplexer multiplexer_3 (.sel(B), .in_0(A[29]), .in_1(A[27]), .out(S[29]));
  Multiplexer multiplexer_4 (.sel(B), .in_0(A[28]), .in_1(A[26]), .out(S[28]));
  Multiplexer multiplexer_5 (.sel(B), .in_0(A[27]), .in_1(A[25]), .out(S[27]));
  Multiplexer multiplexer_6 (.sel(B), .in_0(A[26]), .in_1(A[24]), .out(S[26]));
  Multiplexer multiplexer_7 (.sel(B), .in_0(A[25]), .in_1(A[23]), .out(S[25]));
  Multiplexer multiplexer_8 (.sel(B), .in_0(A[24]), .in_1(A[22]), .out(S[24]));
  Multiplexer multiplexer_9 (.sel(B), .in_0(A[23]), .in_1(A[21]), .out(S[23]));
  Multiplexer multiplexer_10 (.sel(B), .in_0(A[22]), .in_1(A[20]), .out(S[22]));
  Multiplexer multiplexer_11 (.sel(B), .in_0(A[21]), .in_1(A[19]), .out(S[21]));
  Multiplexer multiplexer_12 (.sel(B), .in_0(A[20]), .in_1(A[18]), .out(S[20]));
  Multiplexer multiplexer_13 (.sel(B), .in_0(A[19]), .in_1(A[17]), .out(S[19]));
  Multiplexer multiplexer_14 (.sel(B), .in_0(A[18]), .in_1(A[16]), .out(S[18]));
  Multiplexer multiplexer_15 (.sel(B), .in_0(A[17]), .in_1(A[15]), .out(S[17]));
  Multiplexer multiplexer_16 (.sel(B), .in_0(A[16]), .in_1(A[14]), .out(S[16]));
  Multiplexer multiplexer_17 (.sel(B), .in_0(A[15]), .in_1(A[13]), .out(S[15]));
  Multiplexer multiplexer_18 (.sel(B), .in_0(A[14]), .in_1(A[12]), .out(S[14]));
  Multiplexer multiplexer_19 (.sel(B), .in_0(A[13]), .in_1(A[11]), .out(S[13]));
  Multiplexer multiplexer_20 (.sel(B), .in_0(A[12]), .in_1(A[10]), .out(S[12]));
  Multiplexer multiplexer_21 (.sel(B), .in_0(A[11]), .in_1(A[9]), .out(S[11]));
  Multiplexer multiplexer_22 (.sel(B), .in_0(A[10]), .in_1(A[8]), .out(S[10]));
  Multiplexer multiplexer_23 (.sel(B), .in_0(A[9]), .in_1(A[7]), .out(S[9]));
  Multiplexer multiplexer_24 (.sel(B), .in_0(A[8]), .in_1(A[6]), .out(S[8]));
  Multiplexer multiplexer_25 (.sel(B), .in_0(A[7]), .in_1(A[5]), .out(S[7]));
  Multiplexer multiplexer_26 (.sel(B), .in_0(A[6]), .in_1(A[4]), .out(S[6]));
  Multiplexer multiplexer_27 (.sel(B), .in_0(A[5]), .in_1(A[3]), .out(S[5]));
  Multiplexer multiplexer_28 (.sel(B), .in_0(A[4]), .in_1(A[2]), .out(S[4]));
  Multiplexer multiplexer_29 (.sel(B), .in_0(A[3]), .in_1(A[1]), .out(S[3]));
  Multiplexer multiplexer_30 (.sel(B), .in_0(A[2]), .in_1(A[0]), .out(S[2]));
  Multiplexer multiplexer_31 (.sel(B), .in_0(A[1]), .in_1(1'b0), .out(S[1]));
  Multiplexer multiplexer_32 (.sel(B), .in_0(A[0]), .in_1(1'b0), .out(S[0]));

  assign S[30] = S[31];

  // Other names for the same wires on the sheet: sel = B
endmodule
