// Digital circuit subtrator2.dig as structural Verilog
module subtrator2 (
  input  [31:0] A,
  input  [31:0] B,
  output [31:0] S
);

  wire c0, c1, c2, c4, c5, c5b, c6, c6b, c7, c7b;
  wire [3:0] b0, b1, b2, b3, b4, b5, b6, b7, soma_4bits_1_s, soma_4bits_2_s, soma_4bits_3_s, soma_4bits_4_s,
       soma_4bits_5_s, soma_4bits_6_s, soma_4bits_7_s, soma_4bits_8_s;

  Soma_4bits soma_4bits_1 (.A(A[31:28]), .B(b7), .Cin(c7), .S(soma_4bits_1_s));  // open: Cout
  Soma_4bits soma_4bits_2 (.A(A[31:28]), .B(b7), .Cin(c7b), .S(soma_4bits_2_s));  // open: Cout
  Multiplexer #(.Bits(4)) multiplexer_1 (.sel(c4), .in_0(soma_4bits_1_s), .in_1(soma_4bits_2_s), .out(S[31:28]));
  Soma_4bits soma_4bits_3 (.A(A[27:24]), .B(b6), .Cin(c6b), .S(soma_4bits_3_s), .Cout(c7b));
  assign b5 = ~B[23:20];  // Not not_1, 4 bits wide
  assign b6 = ~B[27:24];  // Not not_2, 4 bits wide
  assign b7 = ~B[31:28];  // Not not_3, 4 bits wide
  Soma_4bits soma_4bits_4 (.A(A[27:24]), .B(b6), .Cin(c6), .S(soma_4bits_4_s), .Cout(c7));
  Soma_4bits soma_4bits_5 (.A(A[23:20]), .B(b5), .Cin(c5b), .S(soma_4bits_5_s), .Cout(c6b));
  Multiplexer #(.Bits(4)) multiplexer_2 (.sel(c4), .in_0(soma_4bits_4_s), .in_1(soma_4bits_3_s), .out(S[27:24]));
  assign b1 = ~B[7:4];  // Not not_4, 4 bits wide
  assign b2 = ~B[11:8];  // Not not_5, 4 bits wide
  assign b3 = ~B[15:12];  // Not not_6, 4 bits wide
  assign b4 = ~B[19:16];  // Not not_7, 4 bits wide
  Soma_4bits soma_4bits_6 (.A(A[23:20]), .B(b5), .Cin(c5), .S(soma_4bits_6_s), .Cout(c6));
  Multiplexer #(.Bits(4)) multiplexer_3 (.sel(c4), .in_0(soma_4bits_6_s), .in_1(soma_4bits_5_s), .out(S[23:20]));
  assign b0 = ~B[3:0];  // Not not_8, 4 bits wide
  Soma_4bits soma_4bits_7 (.A(A[19:16]), .B(b4), .Cin(1'b0), .S(soma_4bits_7_s), .Cout(c5));
  Soma_4bits soma_4bits_8 (.A(A[19:16]), .B(b4), .Cin(1'b1), .S(soma_4bits_8_s), .Cout(c5b));
  Multiplexer #(.Bits(4)) multiplexer_4 (.sel(c4), .in_0(soma_4bits_7_s), .in_1(soma_4bits_8_s), .out(S[19:16]));
  Soma_4bits soma_4bits_9 (.A(A[15:12]), .B(b3), .Cin(c2), .S(S[15:12]), .Cout(c4));
  Soma_4bits soma_4bits_10 (.A(A[11:8]), .B(b2), .Cin(c1), .S(S[11:8]), .Cout(c2));
  Soma_4bits soma_4bits_11 (.A(A[7:4]), .B(b1), .Cin(c0), .S(S[7:4]), .Cout(c1));
  Soma_4bits soma_4bits_12 (.A(A[3:0]), .B(b0), .Cin(1'b1), .S(S[3:0]), .Cout(c0));

  // Other names for the same wires on the sheet: a0[3:0] = A[3:0]; a1[3:0] = A[7:4]; a2[3:0] = A[11:8];
  //   a3[3:0] = A[15:12]; a4[3:0] = A[19:16]; a5[3:0] = A[23:20]; a6[3:0] = A[27:24]; a7[3:0] = A[31:28];
  //   s0[3:0] = S[3:0]; s1[3:0] = S[7:4]; s2[3:0] = S[11:8]; s3[3:0] = S[15:12]; s4[3:0] = S[19:16];
  //   s5[3:0] = S[23:20]; s6[3:0] = S[27:24]; s7[3:0] = S[31:28]
endmodule
